# Fritzing sketch schematic (saved by Fritzing 0.9.2b)
breadboards: 1

parts:
  Part1 = Photon
  LCD1 = Adafruit Positive RGB 2x16 LCD
  DS1 = DS18B20 1-Wire Temperature Sensor [part_number=DS18B20]
  POT1 = Breadboard Trimpot
  R1 = Resistor [tolerance=±5% resistance=10k package=THT]
  R2 = Resistor [tolerance=±5% resistance=4.7k package=THT]
  S1 = Pushbutton [package="[THT]"]
  J1 = Piezo Speaker
  LCD2 = Adafruit Positive RGB 2x16 LCD  # not connected

nets:
  N1: Part1.A0, LCD1.no_name_yet#3
  N2: Part1.A1, LCD1.no_name_yet#5
  N3: Part1.A2, LCD1.no_name_yet#11
  N4: Part1.A4, R1.Pin_0, S1.Pin_1, S1.Pin_2
  N5: Part1.A5, DS1.DQ, R2.Pin_1
  GND: Part1.GND, LCD1.no_name_yet#0, LCD1.no_name_yet#4, DS1.GND, POT1.PIN1, S1.Pin_3, S1.Pin_4, J1.pin1
  VIN: Part1.VIN, LCD1.no_name_yet#1, LCD1.no_name_yet#14, DS1.VDD, POT1.PIN3, R1.Pin_1, R2.Pin_0
  N6: Part1.D0, J1.pin2
  N7: Part1.D1, LCD1.no_name_yet#15
  N8: Part1.D2, LCD1.no_name_yet#16
  N9: Part1.D3, LCD1.no_name_yet#17
  N10: Part1.D4, LCD1.no_name_yet#10
  N11: Part1.D5, LCD1.no_name_yet#12
  N12: Part1.D6, LCD1.no_name_yet#13
  N13: LCD1.no_name_yet#2, POT1.PIN2

custom parts:
  Adafruit Positive RGB 2x16 LCD: Adafruit Positive 2x16 LCD Display with RGB Backlight
